# Fritzing sketch proyecto final (saved by Fritzing 0.9.2b)

parts:
  Parte1 = Adafruit BME280
  U1 = NodeMCU V1.0
  TP4056 = TP4056 [chip_label=TP4056 package="DIP (Dual Inline) [THT]"]
  BATERIA_LIPO_3'7_v = 18650 battery holder [package=battery-18650-kit]
  U2 = Voltage Regulator -- 3.3 V -- LM1117
  Placa_solar_GH165X135 = Solar Cell
  C11 = Electrolytic Capacitor [capacitance=100nF package="100 mil [THT, electrolytic]"]
  C12 = Electrolytic Capacitor [capacitance=10nF package="100 mil [THT, electrolytic]"]

nets:
  3.3V: Parte1.3.3V, U1.3V3, U2.OUT, C11.+
  GND: Parte1.GND, U1.GND, TP4056.pin6, U2.GND, C11.-, C12.-
  N1: Parte1.SCK/SCL, U1.D1
  N2: Parte1.SDO/ADR, U1.D4
  N3: Parte1.SDI/SDA, U1.D2
  N4: Parte1.CS, U1.D3
  N5: U1.D0, U1.RST
  N6: TP4056.pin1, Placa_solar_GH165X135.+
  N7: TP4056.pin2, Placa_solar_GH165X135.-
  N8: TP4056.pin3, U2.IN, C12.+
  N9: TP4056.pin4, BATERIA_LIPO_3'7_v.+
  N10: TP4056.pin5, BATERIA_LIPO_3'7_v.-

custom parts:
  Adafruit BME280: Bosch has stepped up their game with their new BME280 sensor, an environmental sensor with temperature, barometric pressure and humidity! This sensor is great for all sorts of weather/environmental sensing and can even be used in both I2C and SPI! This precision sensor from Bosch is the best low-cost sensing solution for measuring humidity with ±3% accuracy, barometric pressure with ±1 hPa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
  NodeMCU V1.0: ESP8266 based NodeMCU
  TP4056: A DIP stand-in part for whatever IC you want. With 6 pins on a 300mil dual inline package (DIP) footprint.
  18650 battery holder: 18650 Battery Holder
  Voltage Regulator -- 3.3 V -- LM1117: LM1117-3.3 Voltage regulator, 3.3 V output. Note that the pinout order is not the same as LM7805 or LM7833.
